// Logisim project s-mips.circ as structural Verilog
module S_MIPS_Board (
  input  DESHABILITAR_DISPATCHER,
  output halt
);

  wire button_1_out, CLK, CS, d_ff_1_q, LCLR, LoadRAM, LoadRAMOn, LW, R_R_W, R_W, ram_dispatcher_1_finished,
       RCS, Reset_out, RST, TTY_EN;
  wire [2:0] KDB;
  wire [3:0] LMask, Mask, ram_1_read_time, ram_1_write_time, RMask;
  wire [6:0] KDB_DATA, TTY_DATA;
  wire [15:0] Addr, LAddr, RAddr;
  wire [31:0] I0, I1, I2, I3, LData, ram_1_data_out_0, ram_1_data_out_1, ram_1_data_out_2, ram_1_data_out_3,
       RI0, RI1, RI2, RI3;

  TTY #(.rows(25), .cols(80)) tty_1 (.data(TTY_DATA), .clk(CLK), .we(TTY_EN), .clr(RST));
  not not_1 (LoadRAMOn, ram_dispatcher_1_finished);
  RAM_Dispatcher ram_dispatcher_1 (
    .WriteTime(ram_1_write_time), .Clock(CLK), .Data(LData), .Address(LAddr), .Mask(LMask),
    .Finished(ram_dispatcher_1_finished), .Write(LW), .CLR(LCLR));
  Keyboard #(.buflen(64)) keyboard_1 (.clk(CLK), .re(KDB[0]), .avail(KDB[2]), .data(KDB_DATA));  // open: clr
  RAM ram_1 (
    .Address(RAddr), .Data_Out_0(ram_1_data_out_0), .Data_Out_1(ram_1_data_out_1),
    .Data_Out_2(ram_1_data_out_2), .Data_Out_3(ram_1_data_out_3), .Data_In_0(RI0), .Data_In_1(RI1),
    .Data_In_2(RI2), .Data_In_3(RI3), .Mask(RMask), .nRead_Write(R_R_W), .Chip_Select(RCS),
    .Read_Time(ram_1_read_time), .Reset(button_1_out), .Write_Time(ram_1_write_time));
  Button button_1 (.out(button_1_out));
  D_Flip_Flop d_ff_1 (.clk(CLK), .D(1'b1), .Q(d_ff_1_q), .reset(Reset_out));  // open: Qn, preset, en
  Button Reset (.out(Reset_out));
  S_MIPS s_mips_1 (
    .Kbd_Enable(KDB[0]), .Address(Addr), .Kbd_Clear(KDB[1]), .Kbd_Available(KDB[2]), .RAM_In_0(I0),
    .Kbd_ASCII_Data(KDB_DATA), .RAM_In_1(I1), .TTY_Enable(TTY_EN), .RAM_In_2(I2), .RAM_In_3(I3),
    .TTY_ASCII_Data(TTY_DATA), .Reset(RST), .RAM_Out_0(ram_1_data_out_0), .Clock(CLK),
    .RAM_Out_1(ram_1_data_out_1), .Stop(halt), .RAM_Out_2(ram_1_data_out_2), .RAM_Out_3(ram_1_data_out_3),
    .Mask(Mask), .Read_Time(ram_1_read_time), .Write_Time(ram_1_write_time), .nRead_Write(R_W),
    .Chip_Select(CS));
  D_Flip_Flop d_ff_2 (.clk(CLK), .D(d_ff_1_q), .Qn(LCLR), .reset(Reset_out));  // open: Q, preset, en
  or or_1 (RST, LCLR, LoadRAM);
  Clock clock_1 (.out(CLK));
  Multiplexer #(.width(32), .enable("false")) multiplexer_1 (.in0(I0), .in1(LData), .out(RI0), .sel(LoadRAM));
  Multiplexer #(.width(32), .enable("false")) multiplexer_2 (.in0(I1), .in1(LData), .out(RI1), .sel(LoadRAM));
  Multiplexer #(.width(32), .enable("false")) multiplexer_3 (.in0(I2), .in1(LData), .out(RI2), .sel(LoadRAM));
  Multiplexer #(.width(32), .enable("false")) multiplexer_4 (.in0(I3), .in1(LData), .out(RI3), .sel(LoadRAM));
  and and_1 (LoadRAM, ~DESHABILITAR_DISPATCHER, LoadRAMOn);  // AND_Gate
  Multiplexer #(.width(16), .enable("false")) multiplexer_5 (.in0(Addr), .in1(LAddr), .out(RAddr), .sel(LoadRAM));
  Multiplexer #(.width(4), .enable("false")) multiplexer_6 (.in0(Mask), .in1(LMask), .out(RMask), .sel(LoadRAM));
  Multiplexer #(.enable("false")) multiplexer_7 (.in0(CS), .in1(LW), .out(RCS), .sel(LoadRAM));
  Multiplexer #(.enable("false")) multiplexer_8 (.in0(R_W), .in1(LW), .out(R_R_W), .sel(LoadRAM));

  // Notes on the sheet:
  //   NO MODIFICAR
  //   Keyboard
endmodule

module RAM (
  input  [15:0] Address,
  input  [31:0] Data_In_0,
  input  [31:0] Data_In_1,
  input  [31:0] Data_In_2,
  input  [31:0] Data_In_3,
  input  [3:0] Mask,
  input  nRead_Write,
  input  Chip_Select,
  input  Reset,
  output [31:0] Data_Out_0,
  output [31:0] Data_Out_1,
  output [31:0] Data_Out_2,
  output [31:0] Data_Out_3,
  output [3:0] Read_Time,
  output [3:0] Write_Time
);

  wire and_2_out, and_3_out, and_4_out, and_5_out, and_6_out, and_7_out, and_8_out, and_9_out, Changed, CLK,
       comparator_2_eq, comparator_3_eq, comparator_4_eq, comparator_5_eq, comparator_6_eq, Count,
       demultiplexer_3_out0, Idle, Idle_q, Load, Load0, Load1, nand_1_out, or_1_out, or_2_out, or_3_out,
       or_4_out, or_5_out, or_6_out, or_7_out, or_8_out, or_9_out, or_10_out, Proc_q, Update_Mem, Zero_Time;
  wire [3:0] counter_1_q, multiplexer_1_out, subtractor_1_out;
  wire [31:0] register_1_q, register_2_q, register_3_q, register_4_q, register_5_q;

  // Probe on 4'b0011
  // Probe on 4'b0010
  Multiplexer #(.width(4), .enable("false")) multiplexer_1 (
    .in0(4'b0011), .in1(4'b0010), .out(multiplexer_1_out), .sel(nRead_Write));
  or or_1 (or_1_out, Idle, Update_Mem);
  or or_2 (or_2_out, ~Chip_Select, Reset);  // OR_Gate
  Subtractor #(.width(4)) subtractor_1 (.a(multiplexer_1_out), .b(4'b0010), .out(subtractor_1_out));  // open: bin, bout
  D_Flip_Flop u_Idle (.clk(CLK), .D(or_1_out), .Q(Idle_q), .preset(or_2_out));  // open: Qn, en, reset
  Demultiplexer #(.enable("false")) demultiplexer_1 (.out0(Idle), .out1(Load0), .in(Idle_q), .sel(Changed));
  // Probe on counter_1_q
  Counter #(.width(4), .max('hf)) counter_1 (
    .load(Load), .D(subtractor_1_out), .count(Count), .Q(counter_1_q), .clk(CLK), .clr(or_3_out));  // open: carry
  or or_3 (or_3_out, ~Chip_Select, Reset);  // OR_Gate
  Comparator #(.width(4), .mode("unsigned")) comparator_1 (
    .a(4'b0000), .b(counter_1_q), .eq(Zero_Time));  // open: gt, lt
  or or_4 (or_4_out, Count, Load0, Load1);
  Register #(.width(32)) register_1 (.D(Data_In_0), .en(Chip_Select), .Q(register_1_q), .clk(CLK), .clr(or_5_out));
  or or_5 (or_5_out, ~Chip_Select, Reset);  // OR_Gate
  Register #(.width(32)) register_2 (.D(Data_In_1), .en(Chip_Select), .Q(register_2_q), .clk(CLK), .clr(or_6_out));
  or or_6 (or_6_out, ~Chip_Select, Reset);  // OR_Gate
  Register #(.width(32)) register_3 (.D(Data_In_2), .en(Chip_Select), .Q(register_3_q), .clk(CLK), .clr(or_7_out));
  or or_7 (or_7_out, ~Chip_Select, Reset);  // OR_Gate
  Register #(.width(32)) register_4 (.D(Data_In_3), .en(Chip_Select), .Q(register_4_q), .clk(CLK), .clr(or_8_out));
  or or_8 (or_8_out, ~Chip_Select, Reset);  // OR_Gate
  Register #(.width(32)) register_5 (
    .D({{11{1'b1}}, nRead_Write, Mask, Address}), .en(Chip_Select), .Q(register_5_q), .clk(CLK),
    .clr(or_9_out));
  or or_9 (or_9_out, ~Chip_Select, Reset);  // OR_Gate
  D_Flip_Flop Proc (.clk(CLK), .D(or_4_out), .Q(Proc_q), .reset(or_10_out));  // open: Qn, preset, en
  or or_10 (or_10_out, ~Chip_Select, Reset);  // OR_Gate
  Demultiplexer #(.enable("false")) demultiplexer_2 (
    .out0(Count), .out1(Update_Mem), .in(demultiplexer_3_out0), .sel(Zero_Time));
  Demultiplexer #(.enable("false")) demultiplexer_3 (
    .out0(demultiplexer_3_out0), .out1(Load1), .in(Proc_q), .sel(Changed));
  Clock clock_1 (.out(CLK));
  Comparator #(.width(32)) comparator_2 (.a(register_1_q), .b(Data_In_0), .eq(comparator_2_eq));  // open: gt, lt
  Comparator #(.width(32)) comparator_3 (.a(register_2_q), .b(Data_In_1), .eq(comparator_3_eq));  // open: gt, lt
  Comparator #(.width(32)) comparator_4 (.a(register_3_q), .b(Data_In_2), .eq(comparator_4_eq));  // open: gt, lt
  Comparator #(.width(32)) comparator_5 (.a(register_4_q), .b(Data_In_3), .eq(comparator_5_eq));  // open: gt, lt
  Comparator #(.width(32)) comparator_6 (
    .a(register_5_q), .b({{11{1'b1}}, nRead_Write, Mask, Address}), .eq(comparator_6_eq));  // open: gt, lt
  nand nand_1 (nand_1_out, comparator_6_eq, comparator_2_eq, comparator_3_eq, comparator_4_eq, comparator_5_eq);
  and and_1 (Changed, nand_1_out, Chip_Select);
  or or_11 (Load, Count, Load1, Load0);
  and and_2 (and_2_out, Mask[0], Update_Mem, nRead_Write);
  and and_3 (and_3_out, Mask[1], Update_Mem, nRead_Write);
  and and_4 (and_4_out, Mask[2], Update_Mem, nRead_Write);
  and and_5 (and_5_out, Mask[3], Update_Mem, nRead_Write);
  RAM_part #(.addrWidth(16), .dataWidth(32), .bus("separate")) ram_1 (
    .addr(Address), .din(Data_In_0), .data(Data_Out_0), .str(and_2_out), .sel(Chip_Select), .clk(CLK),
    .ld(and_6_out), .clr(Reset));
  and and_6 (and_6_out, ~nRead_Write, Idle);  // AND_Gate
  RAM_part #(.addrWidth(16), .dataWidth(32), .bus("separate")) ram_2 (
    .addr(Address), .din(Data_In_1), .data(Data_Out_1), .str(and_3_out), .sel(Chip_Select), .clk(CLK),
    .ld(and_7_out), .clr(Reset));
  and and_7 (and_7_out, ~nRead_Write, Idle);  // AND_Gate
  RAM_part #(.addrWidth(16), .dataWidth(32), .bus("separate")) ram_3 (
    .addr(Address), .din(Data_In_2), .data(Data_Out_2), .str(and_4_out), .sel(Chip_Select), .clk(CLK),
    .ld(and_8_out), .clr(Reset));
  and and_8 (and_8_out, ~nRead_Write, Idle);  // AND_Gate
  RAM_part #(.addrWidth(16), .dataWidth(32), .bus("separate")) ram_4 (
    .addr(Address), .din(Data_In_3), .data(Data_Out_3), .str(and_5_out), .sel(Chip_Select), .clk(CLK),
    .ld(and_9_out), .clr(Reset));
  and and_9 (and_9_out, ~nRead_Write, Idle);  // AND_Gate

  assign Read_Time = 4'b0011;
  assign Write_Time = 4'b0010;

  // Other names for the same wires on the sheet: M0 = Mask[0]; M1 = Mask[1]; M2 = Mask[2]; M3 = Mask[3];
  //   RW = nRead_Write; CLR = Reset; CS = Chip_Select; Load2 = Count

  // Notes on the sheet:
  //   NO MODIFICAR
  //   excepto quizás los valores RT y WT
  //   BANK0
  //   BANK1
  //   BANK2
  //   BANK3
endmodule

module RAM_Dispatcher (
  input  [3:0] WriteTime,
  input  Clock,
  input  CLR,
  output [31:0] Data,
  output [15:0] Address,
  output [3:0] Mask,
  output Finished,
  output Write
);

  wire demultiplexer_2_out1, demultiplexer_3_out1, End, IDLE_q, IncAddr, Load, or_1_out, or_2_out, While_q,
       WriteEnd;
  wire [3:0] counter_1_q;
  wire [31:0] CurrentAddress_q;

  Counter #(.width(32), .max('hffffffff)) CurrentAddress (
    .count(IncAddr), .Q({CurrentAddress_q[31:18], Address, CurrentAddress_q[1:0]}), .clk(Clock), .clr(CLR));  // open: load, D, carry
  or or_1 (or_1_out, IncAddr, demultiplexer_3_out1, Finished);
  D_Flip_Flop IDLE (.clk(Clock), .D(or_1_out), .Q(IDLE_q), .preset(CLR));  // open: Qn, en, reset
  Demultiplexer #(.enable("false")) demultiplexer_1 (.out0(Load), .out1(Finished), .in(IDLE_q), .sel(End));
  D_Flip_Flop While (.clk(Clock), .D(or_2_out), .Q(While_q), .reset(CLR));  // open: Qn, preset, en
  or or_2 (or_2_out, Write, Load);
  RAM_part #(.addrWidth(18), .dataWidth(32)) ram_1 (
    .addr({Address, CurrentAddress_q[1:0]}), .data(Data), .clk(Clock));  // open: sel, ld, clr
  Demultiplexer #(.enable("false")) demultiplexer_2 (
    .out0(Write), .out1(demultiplexer_2_out1), .in(While_q), .sel(WriteEnd));
  Decoder #(.select(2)) decoder_1 (
    .out0(Mask[0]), .out1(Mask[1]), .out2(Mask[2]), .out3(Mask[3]), .sel(CurrentAddress_q[1:0]));  // open: en
  Demultiplexer #(.enable("false")) demultiplexer_3 (
    .out0(IncAddr), .out1(demultiplexer_3_out1), .in(demultiplexer_2_out1), .sel(End));
  Counter #(.width(4), .max('hf)) counter_1 (
    .load(Load), .D(WriteTime), .count(Write), .Q(counter_1_q), .clk(Clock));  // open: carry, clr
  Comparator #(.width(32)) comparator_1 (.a(Data), .b({32{1'b1}}), .eq(End));  // open: gt, lt
  Comparator #(.width(4)) comparator_2 (.a(4'b0000), .b(counter_1_q), .eq(WriteEnd));  // open: gt, lt

  // Other names for the same wires on the sheet: CLK = Clock; Count = Write; WT[3:0] = WriteTime
endmodule

module S_MIPS (
  input  [31:0] RAM_Out_0,
  input  Kbd_Available,
  input  Reset,
  input  [6:0] Kbd_ASCII_Data,
  input  [31:0] RAM_Out_1,
  input  Clock,
  input  [31:0] RAM_Out_2,
  input  [31:0] RAM_Out_3,
  input  [3:0] Read_Time,
  input  [3:0] Write_Time,
  output TTY_Enable,
  output Kbd_Enable,
  output [6:0] TTY_ASCII_Data,
  output [31:0] RAM_In_0,
  output Kbd_Clear,
  output [31:0] RAM_In_1,
  output Stop,
  output [31:0] RAM_In_2,
  output [31:0] RAM_In_3,
  output [15:0] Address,
  output nRead_Write,
  output Chip_Select,
  output [3:0] Mask
);

  wire branch_control_1_compare_to_zero, control_unit_1_alu_a_selector, control_unit_1_save_alu_result,
       control_unit_1_take_direct_alu_op, control_unit_1_write_rf, control_unit_1_write_sp, Equals,
       instruction_decoder_1_immediate, instruction_decoder_1_jmp, instruction_decoder_1_nlo_hi,
       instruction_decoder_1_npush_pop, instruction_decoder_1_nread_write,
       instruction_decoder_1_nread_write_memory, instruction_decoder_1_write_rd, Stack, try_jmp, Update_PC,
       WI;
  wire [1:0] Addr, control_unit_1_alu_b_selector, instruction_decoder_1_jump_value_selector;
  wire [2:0] control_unit_1_data_in_selector, instruction_decoder_1_jump_type,
       instruction_decoder_1_operation_type;
  wire [4:0] instruction_decoder_1_rd, instruction_decoder_1_rs, instruction_decoder_1_rt;
  wire [5:0] instruction_decoder_1_func_code, instruction_decoder_1_op_code;
  wire [15:0] instruction_decoder_1_offset;
  wire [31:0] ALU_out, ALU_res, instruction_decoder_1_jump_value, multiplexer_1_out, multiplexer_2_out,
       n16_to_32_bit_sign_extender_1_out, n16_to_32_bit_sign_extender_1_outx4, PC, RAM_Out, RF_B;
  wire [31:7] RF_A;

  Instruction_Decoder instruction_decoder_1 (
    .Instruction(RAM_Out), .Write_Insruction(WI), .jmp(instruction_decoder_1_jmp),
    .Jump_value(instruction_decoder_1_jump_value), .Program_Counter__updated(PC),
    .Jump_type(instruction_decoder_1_jump_type), .Rs(instruction_decoder_1_rs),
    .Rt(instruction_decoder_1_rt), .Rd(instruction_decoder_1_rd), .Offset(instruction_decoder_1_offset),
    .nRead_Write(instruction_decoder_1_nread_write), .Write_Rd(instruction_decoder_1_write_rd),
    .Jump_Value_selector(instruction_decoder_1_jump_value_selector),
    .Immediate(instruction_decoder_1_immediate), .nLo_Hi(instruction_decoder_1_nlo_hi), .Clock(Clock),
    .nPush_Pop(instruction_decoder_1_npush_pop),
    .nRead_Write_Memory(instruction_decoder_1_nread_write_memory),
    .Operation_Type(instruction_decoder_1_operation_type), .Op_Code(instruction_decoder_1_op_code),
    .Func_Code(instruction_decoder_1_func_code), .Reset(Reset));
  Multiplexer #(.select(2), .width(32), .enable("false")) multiplexer_1 (
    .in0(instruction_decoder_1_jump_value), .in1(ALU_res), .in2({RF_A, TTY_ASCII_Data}),
    .out(multiplexer_1_out), .sel(instruction_decoder_1_jump_value_selector));  // open: in3
  Branch_Control branch_control_1 (
    .Jump_operation(instruction_decoder_1_jmp), .Jump_value(multiplexer_1_out),
    .Jump_selector(instruction_decoder_1_jump_type), .Next_Program_Counter_Value(ALU_res),
    .Program_Counter(PC), .ALU_Less(ALU_out[0]), .Compare_to_zero(branch_control_1_compare_to_zero),
    .ALU_Equals(Equals), .Clock(Clock), .Reset(Reset), .Update_PC(Update_PC), .Try_Jump(try_jmp));
  _16_to_32_bit_sign_extender u_16_to_32_bit_sign_extender_1 (
    .in_1(instruction_decoder_1_offset), .Outx4(n16_to_32_bit_sign_extender_1_outx4),
    .Out(n16_to_32_bit_sign_extender_1_out));
  Control_Unit control_unit_1 (
    .kbd_Available(Kbd_Available), .Clock(Clock), .Start(1'b1),
    .Operation(instruction_decoder_1_operation_type), .Read_RAM(Read_Time),
    .nR_W_Mem(instruction_decoder_1_nread_write_memory), .Immediate(instruction_decoder_1_immediate),
    .nLo_Hi(instruction_decoder_1_nlo_hi), .nPush_Pop(instruction_decoder_1_npush_pop),
    .Write_RAM(Write_Time), .ALU_A_Selector(control_unit_1_alu_a_selector),
    .ALU_B_Selector(control_unit_1_alu_b_selector), .Write_Instruction(WI), .Update_PC(Update_PC),
    .Take_Direct_ALU_Op(control_unit_1_take_direct_alu_op), .Save_ALU_Result(control_unit_1_save_alu_result),
    .Write_SP(control_unit_1_write_sp), .Access_SP(Stack),
    .Data_In_Selector(control_unit_1_data_in_selector), .Keybord_Enable(Kbd_Enable), .TTY_Enable(TTY_Enable),
    .End(Stop), .Reset(Reset), .Chip_Select(Chip_Select), .RAM_Address_Selector(Addr),
    .Write_RF(control_unit_1_write_rf), .Write_RAM_2(nRead_Write), .Try_jump(try_jmp));
  Multiplexer #(.select(2), .width(32), .enable("false")) multiplexer_2 (
    .in0(PC), .in1(ALU_res), .in2({RF_A, TTY_ASCII_Data}), .out(multiplexer_2_out), .sel(Addr));  // open: in3
  Access_Memory access_memory_1 (
    .Target_Address(multiplexer_2_out), .RAM_O0(RAM_Out_0), .RAM_O1(RAM_Out_1), .To_Write(RF_B),
    .RAM_O2(RAM_Out_2), .RAM_O3(RAM_Out_3), .Address(Address), .Mask(Mask), .RAM_I0(RAM_In_0),
    .RAM_I1(RAM_In_1), .RAM_out(RAM_Out), .RAM_I2(RAM_In_2), .RAM_I3(RAM_In_3));
  Data_Path data_path_1 (
    .Program_Counter_Value(PC), .Rs(instruction_decoder_1_rs), .Rt(instruction_decoder_1_rt),
    .Rd(instruction_decoder_1_rd), .RW(instruction_decoder_1_nread_write),
    .nRt_Rd(instruction_decoder_1_write_rd), .Clock(Clock), .Offset(n16_to_32_bit_sign_extender_1_out),
    .Offset_x4(n16_to_32_bit_sign_extender_1_outx4), .Compare_to_zero(branch_control_1_compare_to_zero),
    .ALU_out(ALU_out), .ALU_Result(ALU_res), .Op_Code(instruction_decoder_1_op_code),
    .Func_Code(instruction_decoder_1_func_code), .RF_A({RF_A, TTY_ASCII_Data}), .Equals(Equals),
    .Memory_Input(RAM_Out), .KBD_Data(Kbd_ASCII_Data), .Reset(Reset),
    .ALU_A_Selector(control_unit_1_alu_a_selector), .ALU_B_Selector(control_unit_1_alu_b_selector),
    .Save_ALU_Result(control_unit_1_save_alu_result), .ALU_Sum(control_unit_1_take_direct_alu_op),
    .Access_SP(Stack), .DI_Selector(control_unit_1_data_in_selector), .Write_SP(control_unit_1_write_sp),
    .RF_B(RF_B), .Write_Register_FIle(control_unit_1_write_rf));

  // Other names for the same wires on the sheet: CLK = Clock; CLR = Reset; CS = Chip_Select;
  //   KBD_AVAIL = Kbd_Available; KBD_CLR = Kbd_Clear; KBD_DATA[6:0] = Kbd_ASCII_Data; RAM_A[15:0] = Address;
  //   RAM_INPUT_0[31:0] = RAM_In_0; RAM_INPUT_1[31:0] = RAM_In_1; RAM_INPUT_2[31:0] = RAM_In_2;
  //   RAM_INPUT_3[31:0] = RAM_In_3; RAM_MASK[3:0] = Mask; RAM_OUTPUT_0[31:0] = RAM_Out_0;
  //   RAM_OUTPUT_1[31:0] = RAM_Out_1; RAM_OUTPUT_2[31:0] = RAM_Out_2; RAM_OUTPUT_3[31:0] = RAM_Out_3;
  //   RF_A[6:0] = TTY_ASCII_Data; TTY_DATA[6:0] = TTY_ASCII_Data; RW = nRead_Write

  // Notes on the sheet:
  //   Inputs
  //   DATA FROM RAM
  //   RAM TIMING
  //   RAM
  //   Outputs
  //   DATA TO RAM
  //   RAM ADDRESS
  //   DATA WRITE MASK
  //   RAM CONTROL
  //   KEYBOARD
  //   Misc
  //   TTY
  //   SEQUENCING
endmodule

module Access_Memory (
  input  [31:0] Target_Address,
  input  [31:0] RAM_O0,
  input  [31:0] RAM_O1,
  input  [31:0] To_Write,
  input  [31:0] RAM_O2,
  input  [31:0] RAM_O3,
  output [15:0] Address,
  output [3:0] Mask,
  output [31:0] RAM_I0,
  output [31:0] RAM_I1,
  output [31:0] RAM_out,
  output [31:0] RAM_I2,
  output [31:0] RAM_I3
);

  wire [1:0] divider_1_out;
  wire [31:2] divider_1_out_2;
  wire [31:16] divider_2_out;

  Divider #(.width(32)) divider_1 (
    .a(Target_Address), .b(32'h4), .out({divider_1_out_2, divider_1_out}));  // open: upper, rem
  Multiplexer #(.select(2), .width(32), .enable("false")) multiplexer_1 (
    .in0(RAM_O0), .in1(RAM_O1), .in2(RAM_O2), .in3(RAM_O3),
    .out({RAM_out[7:0], RAM_out[15:8], RAM_out[23:16], RAM_out[31:24]}), .sel(divider_1_out));
  Divider #(.width(32)) divider_2 (
    .a({divider_1_out_2, divider_1_out}), .b(32'h4), .out({divider_2_out, Address}));  // open: upper, rem
  Decoder #(.select(2), .enable("false")) decoder_1 (
    .out0(Mask[0]), .out1(Mask[1]), .out2(Mask[2]), .out3(Mask[3]), .sel(divider_1_out));

  assign RAM_I0 = {To_Write[7:0], To_Write[15:8], To_Write[23:16], To_Write[31:24]};
  assign RAM_I1 = {To_Write[7:0], To_Write[15:8], To_Write[23:16], To_Write[31:24]};
  assign RAM_I2 = {To_Write[7:0], To_Write[15:8], To_Write[23:16], To_Write[31:24]};
  assign RAM_I3 = {To_Write[7:0], To_Write[15:8], To_Write[23:16], To_Write[31:24]};
endmodule

module Control_Unit (
  input  Start,
  input  Immediate,
  input  Reset,
  input  nLo_Hi,
  input  Clock,
  input  nPush_Pop,
  input  [2:0] Operation,
  input  kbd_Available,
  input  nR_W_Mem,
  input  [3:0] Read_RAM,
  input  [3:0] Write_RAM,
  output End,
  output TTY_Enable,
  output Keybord_Enable,
  output ALU_A_Selector,
  output Access_SP,
  output Write_SP,
  output [1:0] ALU_B_Selector,
  output [2:0] Data_In_Selector,
  output Save_ALU_Result,
  output Take_Direct_ALU_Op,
  output Write_RF,
  output Chip_Select,
  output [1:0] RAM_Address_Selector,
  output Write_Instruction,
  output Update_PC,
  output Write_RAM_2,
  output Try_jump
);

  wire ALU_4_2, ALU_A_1, ALU_A_3, ALU_B_1, ALU_OS_1, ALU_OS_x4, and_1_out, and_2_out, and_3_out, and_4_out,
       and_5_out, chronometer_1_cicle_finished, CLK_CHR, demultiplexer_1_out0, demultiplexer_1_out1,
       demultiplexer_2_out0, demultiplexer_2_out1, demultiplexer_2_out2, demultiplexer_2_out3,
       demultiplexer_2_out4, demultiplexer_2_out5, demultiplexer_2_out6, demultiplexer_2_out7, End_Inst, mem,
       Memory_2, minus_1, or_1_out, or_3_out, or_5_out, or_7_out, or_8_out, or_9_out, or_15_out, preF,
       S2___Read_RF__operators_2_q, S2___Read_RF__SP___Rs_q, S2__Read_RF__char_q, S2__Read_RF__operators_q,
       S5__Wait_for_memory_q, S9__Read_kbd_buffer_q, S10__End_q, S11__IDLE_q, SP, WHi, WLo, WRF_4;
  wire [3:0] Mem_Time, multiplexer_1_out;

  or or_1 (or_1_out, demultiplexer_2_out7, Reset);
  D_Flip_Flop #(.trigger("falling")) S10__End (
    .clk(Clock), .D(demultiplexer_2_out7), .Q(S10__End_q), .en(or_1_out), .reset(Reset));  // open: Qn, preset
  D_Flip_Flop #(.trigger("falling")) S11__IDLE (
    .clk(Clock), .D(S10__End_q), .Q(S11__IDLE_q), .preset(Reset));  // open: Qn, en, reset
  Multiplexer #(.width(4), .enable("false")) multiplexer_1 (
    .in0(Mem_Time), .in1(Read_RAM), .out(multiplexer_1_out), .sel(Write_Instruction));
  Multiplexer #(.width(4), .enable("false")) multiplexer_2 (
    .in0(Read_RAM), .in1(Write_RAM), .out(Mem_Time), .sel(nR_W_Mem));
  and and_1 (and_1_out, S11__IDLE_q, Start);
  or or_2 (preF, and_1_out, End_Inst);
  Chronometer chronometer_1 (
    .in_2(1'b1), .in_3(or_3_out), .in_4(multiplexer_1_out), .Cicle_Finished(chronometer_1_cicle_finished),
    .in_1(Clock));  // open: Counting
  or or_3 (or_3_out, ALU_A_3, preF, ALU_4_2);
  Demultiplexer #(.disabled(0), .enable("false")) demultiplexer_1 (
    .out0(demultiplexer_1_out0), .out1(demultiplexer_1_out1), .in(Memory_2), .sel(nPush_Pop));
  D_Flip_Flop #(.trigger("falling")) S0__Fetch (
    .clk(CLK_CHR), .D(preF), .Q(Write_Instruction), .reset(Reset));  // open: Qn, preset, en
  or or_4 (End, demultiplexer_2_out7, S10__End_q);
  or or_5 (or_5_out, mem, Write_Instruction, Memory_2);
  // OR_Gate or_6 has open pins: in0=ALU_B_1, in1=Try_jump, out=open
  or or_7 (or_7_out, Write_Instruction, ALU_4_2);
  or or_8 (or_8_out, ALU_OS_1, ALU_A_3);
  or or_9 (or_9_out, mem, demultiplexer_1_out0);
  and and_2 (and_2_out, Memory_2, ~nPush_Pop);  // AND_Gate
  and and_3 (and_3_out, nR_W_Mem, mem);
  D_Flip_Flop #(.trigger("falling")) S1__Decode (
    .clk(CLK_CHR), .D(Write_Instruction), .Q(Update_PC), .reset(Reset));  // open: Qn, preset, en
  Multiplexer #(.enable("false")) multiplexer_3 (
    .in0(Clock), .in1(chronometer_1_cicle_finished), .out(CLK_CHR), .sel(or_5_out));
  or or_10 (ALU_A_Selector, ALU_A_1, Try_jump, ALU_A_3, ALU_4_2);
  Priority_Encoder #(.select(2)) priority_encoder_1 (
    .in0(1'b1), .in1(or_7_out), .in2(or_8_out), .in3(ALU_OS_x4), .out(ALU_B_Selector));  // open: gs, en_out, en_in
  or or_11 (Take_Direct_ALU_Op, Write_Instruction, ALU_OS_x4, ALU_A_3);
  or or_12 (Chip_Select, Memory_2, Write_Instruction, mem);
  Priority_Encoder #(.select(2)) priority_encoder_2 (
    .in0(1'b1), .in1(or_9_out), .in2(demultiplexer_1_out1), .out(RAM_Address_Selector));  // open: in3, gs, en_out, en_in
  or or_13 (Write_RAM_2, and_2_out, and_3_out);
  Demultiplexer #(.select(3), .enable("false")) demultiplexer_2 (
    .out0(demultiplexer_2_out0), .out1(demultiplexer_2_out1), .out2(demultiplexer_2_out2),
    .out3(demultiplexer_2_out3), .out4(demultiplexer_2_out4), .out5(demultiplexer_2_out5),
    .out6(demultiplexer_2_out6), .out7(demultiplexer_2_out7), .in(Update_PC), .sel(Operation));
  or or_14 (Save_ALU_Result, Write_Instruction, ALU_OS_x4, ALU_A_3, ALU_4_2);
  D_Flip_Flop #(.trigger("falling")) S2__Read_RF__operators (
    .clk(Clock), .D(demultiplexer_2_out0), .Q(S2__Read_RF__operators_q), .reset(Reset));  // open: Qn, preset, en
  D_Flip_Flop #(.trigger("falling")) S2___Read_RF__operators (
    .clk(Clock), .D(demultiplexer_2_out1), .Q(ALU_OS_x4), .reset(Reset));  // open: Qn, preset, en
  D_Flip_Flop #(.trigger("falling")) S2___Read_RF__operators_2 (
    .clk(Clock), .D(demultiplexer_2_out2), .Q(S2___Read_RF__operators_2_q), .reset(Reset));  // open: Qn, preset, en
  D_Flip_Flop #(.trigger("falling")) S6__Write__from_Hi_Lo (
    .clk(Clock), .D(demultiplexer_2_out3), .Q(WRF_4), .reset(Reset));  // open: Qn, preset, en
  D_Flip_Flop #(.trigger("falling")) S2___Read_RF__SP___Rs (
    .clk(Clock), .D(demultiplexer_2_out4), .Q(S2___Read_RF__SP___Rs_q), .reset(Reset));  // open: Qn, preset, en
  D_Flip_Flop #(.trigger("falling")) S2__Read_RF__char (
    .clk(Clock), .D(demultiplexer_2_out5), .Q(S2__Read_RF__char_q), .reset(Reset));  // open: Qn, preset, en
  D_Flip_Flop #(.trigger("falling")) S9__Read_kbd_buffer (
    .clk(Clock), .D(demultiplexer_2_out6), .Q(S9__Read_kbd_buffer_q), .reset(Reset));  // open: Qn, preset, en
  or or_15 (or_15_out, mem, Memory_2);
  and and_4 (and_4_out, mem, ~nR_W_Mem);  // AND_Gate
  and and_5 (and_5_out, Memory_2, nPush_Pop);
  D_Flip_Flop #(.trigger("falling")) S3__Operate_and_Write (
    .clk(Clock), .D(S2___Read_RF__operators_2_q), .Q(ALU_A_3), .reset(Reset));  // open: Qn, preset, en
  D_Flip_Flop #(.trigger("falling")) S3__Operate_and_Write_2 (
    .clk(Clock), .D(S2___Read_RF__SP___Rs_q), .Q(ALU_4_2), .reset(Reset));  // open: Qn, preset, en
  D_Flip_Flop #(.trigger("falling")) S8__Write_in_terminal (
    .clk(Clock), .D(S2__Read_RF__char_q), .Q(TTY_Enable), .reset(Reset));  // open: Qn, preset, en
  or or_16 (Write_RF, ALU_A_1, Try_jump, and_4_out, WRF_4, and_5_out);
  D_Flip_Flop #(.trigger("falling")) S3__Operate_and_Write_3 (
    .clk(Clock), .D(S2__Read_RF__operators_q), .Q(ALU_A_1), .reset(Reset));  // open: Qn, preset, en
  D_Flip_Flop #(.trigger("falling")) S3__Operate_and_Write_4 (
    .clk(Clock), .D(ALU_OS_x4), .Q(Try_jump), .reset(Reset));  // open: Qn, preset, en
  Demultiplexer #(.enable("false")) demultiplexer_3 (.out0(WLo), .out1(WHi), .in(WRF_4), .sel(nLo_Hi));
  or or_17 (SP, ALU_4_2, S2___Read_RF__SP___Rs_q);
  Demultiplexer #(.enable("false")) demultiplexer_4 (
    .out0(minus_1), .out1(Keybord_Enable), .in(S9__Read_kbd_buffer_q), .sel(kbd_Available));
  or or_18 (Access_SP, SP, Memory_2);
  Priority_Encoder priority_encoder_3 (
    .in0(1'b1), .in1(Write_SP), .in2(WHi), .in3(WLo), .in4(or_15_out), .in5(Keybord_Enable), .in6(minus_1),
    .out(Data_In_Selector));  // open: in7, en_in, gs, en_out
  Demultiplexer #(.enable("false")) demultiplexer_5 (.out0(ALU_B_1), .out1(ALU_OS_1), .in(ALU_A_1), .sel(Immediate));
  D_Flip_Flop #(.trigger("falling")) S4__Access_memory (
    .clk(CLK_CHR), .D(ALU_A_3), .Q(mem), .reset(Reset));  // open: Qn, preset, en
  D_Flip_Flop #(.trigger("falling")) S4__Access_memory_2 (
    .clk(CLK_CHR), .D(ALU_4_2), .Q(Memory_2), .reset(Reset));  // open: Qn, preset, en
  D_Flip_Flop #(.trigger("falling")) S5__Wait_for_memory (
    .clk(CLK_CHR), .D(mem), .Q(S5__Wait_for_memory_q), .reset(Reset));  // open: Qn, preset, en
  D_Flip_Flop #(.trigger("falling")) S5__Wait_for_memory_2 (
    .clk(CLK_CHR), .D(Memory_2), .Q(Write_SP), .reset(Reset));  // open: Qn, preset, en
  or or_19 (End_Inst, ALU_A_1, Try_jump, S5__Wait_for_memory_q, WRF_4, Write_SP, TTY_Enable, S9__Read_kbd_buffer_q);

  // Other names for the same wires on the sheet: ALU_4_1 = Write_Instruction; ALU_PC_1 = Write_Instruction;
  //   fetch = Write_Instruction; Save_ALU_1 = Write_Instruction; TD_1 = Write_Instruction; WI = Write_Instruction;
  //   Hi = nLo_Hi; Imm = Immediate; ALU_A_2 = Try_jump; ALU_B_2 = Try_jump; jmp = Try_jump; WRF_2 = Try_jump;
  //   KBD_In = Keybord_Enable; kbdA = kbd_Available; Memory_1 = mem; WRF_3 = mem; OP[2:0] = Operation;
  //   Pop = nPush_Pop; ALU_OS_2 = ALU_A_3; preM = ALU_A_3; Save_ALU_3 = ALU_A_3; ALU_A_4 = ALU_4_2; preS = ALU_4_2;
  //   Save_ALU_4 = ALU_4_2; Read_Time[3:0] = Read_RAM; RST = Reset; stack = Memory_2; WRF_5 = Memory_2;
  //   ALU_PC_2 = ALU_OS_x4; Save_ALU_2 = ALU_OS_x4; TD_2 = ALU_OS_x4; UD_PC_1 = Update_PC; ALU_out = ALU_A_1;
  //   WRF_1 = ALU_A_1; ALU_res = Write_SP; WSP = Write_SP

  // Notes on the sheet:
  //   Inputs
  //   Memory Clock
  //   Control Signals
  //   Halt
  //   ALU Signals
  //   Memory Signals
  //   ALU operation
  //   Jump operation
  //   Memory operation
  //   Move operation
  //   Stack operation
  //   Write in terminal
  //   Read keyboard
  //   Outputs
  //   RF Signals
  //   Misc Signals
endmodule

module Instruction_Decoder (
  input  [31:0] Instruction,
  input  Write_Insruction,
  input  Clock,
  input  Reset,
  input  [31:0] Program_Counter__updated,
  output jmp,
  output Write_Rd,
  output nRead_Write,
  output [1:0] Jump_Value_selector,
  output [15:0] Offset,
  output [4:0] Rs,
  output [5:0] Op_Code,
  output [4:0] Rt,
  output [5:0] Func_Code,
  output [31:0] Jump_value,
  output [4:0] Rd,
  output Immediate,
  output nLo_Hi,
  output [2:0] Jump_type,
  output [2:0] Operation_Type,
  output nPush_Pop,
  output nRead_Write_Memory
);

  wire and_3_out, and_4_out, and_5_out, and_6_out, and_8_out, demultiplexer_1_out0, demultiplexer_1_out1,
       halt, IO, J_Type, jmp_t, Memory_Op, Move_Hi_Lo, nand_1_out, NOP, nor_2_out, nor_4_out, nor_6_out,
       nor_7_out, nor_8_out, or_2_out, or_3_out, or_4_out, stack, xor_1_out;

  Register #(.width(32), .trigger("falling")) register_1 (
    .D(Instruction), .en(Write_Insruction), .Q({Op_Code, Rs, Rt, Offset[15:6], Func_Code}), .clk(Clock),
    .clr(Reset));
  xor xor_1 (xor_1_out, Op_Code[3], Op_Code[5]);
  nor nor_1 (Immediate, ~Op_Code[3], Op_Code[4], Op_Code[5]);  // NOR_Gate
  not not_1 (nLo_Hi, Func_Code[1]);
  not not_2 (nPush_Pop, Func_Code[0]);
  Multiplexer #(.enable("false")) multiplexer_1 (
    .in0(Op_Code[3]), .in1(Func_Code[0]), .out(nRead_Write_Memory), .sel(Write_Rd));
  and and_1 (Move_Hi_Lo, Write_Rd, ~Func_Code[3], Func_Code[4], ~Func_Code[5]);  // AND_Gate
  and and_2 (Memory_Op, Op_Code[0], Op_Code[1], ~Op_Code[4], Op_Code[5]);  // AND_Gate
  or or_1 (nRead_Write, Write_Rd, xor_1_out);
  or or_2 (or_2_out, Immediate, nor_2_out);
  nor nor_2 (nor_2_out, Move_Hi_Lo, NOP);
  Demultiplexer #(.enable("false")) demultiplexer_1 (
    .out0(demultiplexer_1_out0), .out1(demultiplexer_1_out1), .in(IO), .sel(Func_Code[2]));
  nor nor_3 (NOP, Func_Code[0], Func_Code[1], Func_Code[2], Func_Code[3], Func_Code[4], Func_Code[5], Offset[6], Offset[7], Offset[8], Offset[9], Offset[10], Offset[11], Offset[12], Offset[13], Offset[14], Offset[15], Rt[1], Rt[2], Rt[3], Rt[4], Rs[0], Rs[1], Rs[2], Rs[3], Rs[4], Op_Code[0], Op_Code[1], Op_Code[2], Op_Code[3], Op_Code[4], Op_Code[5], Rt[0]);
  Priority_Encoder priority_encoder_1 (
    .in0(or_2_out), .in1(jmp_t), .in2(Memory_Op), .in3(Move_Hi_Lo), .in4(stack), .in5(demultiplexer_1_out0),
    .in6(demultiplexer_1_out1), .in7(halt), .out(Operation_Type));  // open: en_in, gs, en_out
  and and_3 (and_3_out, Op_Code[5], Op_Code[4]);
  nor nor_4 (nor_4_out, Op_Code[5], Op_Code[4], Op_Code[3], Op_Code[2], Op_Code[1], Op_Code[0]);
  nor nor_5 (J_Type, Op_Code[0], ~Op_Code[1], Op_Code[2], Op_Code[3], Op_Code[4], Op_Code[5]);  // NOR_Gate
  nand nand_1 (nand_1_out, ~Op_Code[0], Op_Code[1], ~Op_Code[2]);  // NAND_Gate
  or or_3 (or_3_out, Op_Code[0], Op_Code[1], Op_Code[2]);
  nor nor_6 (nor_6_out, Op_Code[3], Op_Code[4], Op_Code[5]);
  and and_4 (and_4_out, Op_Code[0], Op_Code[1], Op_Code[2]);
  and and_5 (and_5_out, Op_Code[3], Op_Code[4], Op_Code[5]);
  and and_6 (and_6_out, Func_Code[0], Func_Code[1], Func_Code[3], Func_Code[4], Func_Code[5]);
  or or_4 (or_4_out, Func_Code[0], Func_Code[2]);
  or or_5 (Write_Rd, and_3_out, nor_4_out);
  and and_7 (Jump_Value_selector[0], nand_1_out, or_3_out, nor_6_out);
  nor nor_7 (nor_7_out, Op_Code[0], Op_Code[1], Op_Code[2]);
  and and_8 (and_8_out, and_4_out, and_5_out);
  and and_9 (stack, nor_7_out, and_5_out);
  and and_10 (halt, and_8_out, and_6_out);
  and and_11 (IO, and_8_out, or_4_out);
  or or_6 (jmp, J_Type, Jump_Value_selector[1], Jump_Value_selector[0]);
  or or_7 (jmp_t, NOP, jmp);
  Multiplexer #(.width(32), .enable("false")) multiplexer_2 (
    .in0(Program_Counter__updated),
    .in1({Program_Counter__updated[31:28], Rs, Rt, Offset[15:6], Func_Code, 2'b00}), .out(Jump_value),
    .sel(J_Type));
  Multiplexer #(.width(3), .enable("false")) multiplexer_3 (
    .in0(Op_Code[2:0]), .in1(3'b000), .out(Jump_type), .sel(J_Type));
  and and_12 (Jump_Value_selector[1], nor_4_out, nor_8_out);
  nor nor_8 (nor_8_out, Func_Code[0], Func_Code[1], Func_Code[2], ~Func_Code[3], Func_Code[4], Func_Code[5]);  // NOR_Gate

  assign Offset[5:0] = Func_Code;
  assign Rd = Offset[15:11];

  // Other names for the same wires on the sheet: Instruction_t[31:0] = {Op_Code, Rs, Rt, Offset[15:6], Func_Code};
  //   PC[31:0] = Program_Counter__updated; branch = Jump_Value_selector[0]; JR = Jump_Value_selector[1];
  //   R_Type = Write_Rd

  // Notes on the sheet:
  //   (ver libreta con analisis)
  //   Instruction
  //   Memory
  //   Register File
  //   En el register file paso como selector del registro a escribir un multiplexer
  //   con Rt y Rd de entradas y este bit (R-Type) como selector
  //   INPUTS
  //   Control Unit
  //   MISC
  //   OUTPUTS
  //   Common
  //   Branch Control
  //   En el branch control se pasa el jump value, el offset trabajado y
  //   el contenido de Rs por un multiplexer con este selector
  //   Si es nop se mantiene el PC, si no se construye la nueva direccion
  //   Selector que usara el branch control
  //   para determinar el tipo de salto
endmodule

module Branch_Control (
  input  Jump_operation,
  input  [31:0] Jump_value,
  input  [2:0] Jump_selector,
  input  [31:0] Next_Program_Counter_Value,
  input  ALU_Less,
  input  ALU_Equals,
  input  Update_PC,
  input  Clock,
  input  Try_Jump,
  input  Reset,
  output [31:0] Program_Counter,
  output Compare_to_zero
);

  wire and_1_out, and_2_out, and_3_out, multiplexer_2_out, not_1_out, not_2_out, or_1_out, or_2_out;
  wire [31:0] multiplexer_1_out;

  and and_1 (and_1_out, Jump_operation, multiplexer_2_out);
  Multiplexer #(.width(32), .enable("false")) multiplexer_1 (
    .in0(Next_Program_Counter_Value), .in1(Jump_value), .out(multiplexer_1_out), .sel(and_1_out));
  or or_1 (or_1_out, and_2_out, Update_PC);
  and and_2 (and_2_out, and_1_out, Try_Jump);
  Multiplexer #(.select(3), .enable("false")) multiplexer_2 (
    .in0(1'b1), .in1(ALU_Less), .in2(1'b1), .in3(1'b0), .in4(ALU_Equals), .in5(not_2_out), .in6(or_2_out),
    .in7(not_1_out), .out(multiplexer_2_out), .sel(Jump_selector));
  not not_1 (not_1_out, or_2_out);
  not not_2 (not_2_out, ALU_Equals);
  or or_2 (or_2_out, ALU_Less, ALU_Equals);
  Register #(.width(32), .trigger("falling")) PC (
    .D(multiplexer_1_out), .en(or_1_out), .Q(Program_Counter), .clk(Clock), .clr(Reset));
  and and_3 (and_3_out, ~Jump_selector[1], Jump_selector[2]);  // AND_Gate
  and and_4 (Compare_to_zero, ~and_3_out, Jump_operation);  // AND_Gate

  // Other names for the same wires on the sheet: CLK = Clock; equal = ALU_Equals; jmp = Jump_operation;
  //   JSel[2:0] = Jump_selector; JV[31:0] = Jump_value; less = ALU_Less; PC[31:0] = Next_Program_Counter_Value;
  //   RST = Reset; try_jmp = Try_Jump; Update = Update_PC

  // Notes on the sheet:
  //   Inputs
  //   Output
endmodule

module Data_Path (
  input  [4:0] Rs,
  input  [31:0] Memory_Input,
  input  [4:0] Rt,
  input  ALU_A_Selector,
  input  [4:0] Rd,
  input  [1:0] ALU_B_Selector,
  input  [6:0] KBD_Data,
  input  RW,
  input  Save_ALU_Result,
  input  Reset,
  input  nRt_Rd,
  input  ALU_Sum,
  input  Clock,
  input  [5:0] Op_Code,
  input  [5:0] Func_Code,
  input  Write_Register_FIle,
  input  Access_SP,
  input  [31:0] Program_Counter_Value,
  input  [31:0] Offset,
  input  [2:0] DI_Selector,
  input  Write_SP,
  input  [31:0] Offset_x4,
  input  Compare_to_zero,
  output Equals,
  output [31:0] ALU_out,
  output [31:0] ALU_Result,
  output [31:0] RF_A,
  output [31:0] RF_B
);

  wire alu_decoder_1_write_hi___lo, and_1_out, or_1_out, WH_L;
  wire [3:0] alu_decoder_1_alu_operation;
  wire [4:0] multiplexer_2_out, multiplexer_3_out, multiplexer_4_out, multiplexer_4_out_2;
  wire [31:0] alu_1_helper_result, bit_extender_1_out, Hi, Lo, multiplexer_1_out, multiplexer_5_out,
       multiplexer_6_out, multiplexer_7_out;

  assign bit_extender_1_out = {{25{KBD_Data[6]}}, KBD_Data};  // Bit_Extender bit_extender_1
  Multiplexer #(.select(3), .width(32), .enable("false")) multiplexer_1 (
    .in0(ALU_out), .in1(ALU_Result), .in2(Hi), .in3(Lo), .in4(Memory_Input), .in5(bit_extender_1_out),
    .in6({32{1'b1}}), .out(multiplexer_1_out), .sel(DI_Selector));  // open: in7
  Multiplexer #(.width(5), .enable("false")) multiplexer_2 (.in0(Rt), .in1(Rd), .out(multiplexer_2_out), .sel(nRt_Rd));
  and and_1 (and_1_out, RW, ~WH_L, Write_Register_FIle);  // AND_Gate
  Multiplexer #(.width(5), .enable("false")) multiplexer_3 (
    .in0(multiplexer_2_out), .in1({5{1'b1}}), .out(multiplexer_3_out), .sel(Write_SP));
  or or_1 (or_1_out, and_1_out, Write_SP);
  Register_File register_file_1 (
    .in_1(multiplexer_4_out_2), .in_2(multiplexer_4_out), .in_3(multiplexer_3_out), .in_4(multiplexer_1_out),
    .in_5(or_1_out), .in_6(Clock), .R1(RF_A), .R2(RF_B), .in_7(Reset));
  Multiplexer #(.width(10), .enable("false")) multiplexer_4 (
    .in0({Rs, Rt}), .in1({{5{1'b1}}, Rs}), .out({multiplexer_4_out_2, multiplexer_4_out}), .sel(Access_SP));
  Multiplexer #(.width(32), .enable("false")) multiplexer_5 (
    .in0(RF_B), .in1({32{1'b0}}), .out(multiplexer_5_out), .sel(Compare_to_zero));
  Multiplexer #(.width(32), .enable("false")) multiplexer_6 (
    .in0(Program_Counter_Value), .in1(RF_A), .out(multiplexer_6_out), .sel(ALU_A_Selector));
  Multiplexer #(.select(2), .width(32), .enable("false")) multiplexer_7 (
    .in0(multiplexer_5_out), .in1(32'h4), .in2(Offset), .in3(Offset_x4), .out(multiplexer_7_out),
    .sel(ALU_B_Selector));
  ALU alu_1 (
    .in_1(multiplexer_6_out), .in_2(multiplexer_7_out), .in_3(alu_decoder_1_alu_operation), .Equal(Equals),
    .Result(ALU_out), .Helper_Result(alu_1_helper_result));  // open: Overflow, Carry_Flag, Zero_Flag
  ALU_Decoder alu_decoder_1 (
    .Func_Code(Func_Code), .ALU_operation(alu_decoder_1_alu_operation), .Op_Code(Op_Code),
    .Write_Hi___Lo(alu_decoder_1_write_hi___lo), .Sum(ALU_Sum));
  and and_2 (WH_L, Write_Register_FIle, alu_decoder_1_write_hi___lo);
  Register #(.width(32)) u_Lo (.D(ALU_out), .en(WH_L), .Q(Lo), .clk(Clock), .clr(Reset));
  Register #(.width(32)) Res (.D(ALU_out), .en(Save_ALU_Result), .Q(ALU_Result), .clk(Clock), .clr(Reset));
  Register #(.width(32)) u_Hi (.D(alu_1_helper_result), .en(WH_L), .Q(Hi), .clk(Clock), .clr(Reset));

  // Other names for the same wires on the sheet: A[31:0] = RF_A; A_Sel = ALU_A_Selector; B[31:0] = RF_B;
  //   B_Sel[1:0] = ALU_B_Selector; CLK = Clock; DI_Sel[2:0] = DI_Selector; FC[5:0] = Func_Code; kbd_D[6:0] = KBD_Data;
  //   Mem_In[31:0] = Memory_Input; OC[5:0] = Op_Code; Os[31:0] = Offset; Osx4[31:0] = Offset_x4;
  //   PC[31:0] = Program_Counter_Value; RST = Reset; Save_ALU = Save_ALU_Result; SP = Access_SP; tunnel = ALU_Sum;
  //   WRF = Write_Register_FIle; WSP = Write_SP; Zero = Compare_to_zero

  // Notes on the sheet:
  //   S-MIPS
  //   Branch Control
  //   Inputs
  //   Control Unit
  //   Instruction Decoder
  //   Outputs
endmodule

module ALU (
  input  [31:0] in_1,
  input  [31:0] in_2,
  input  [3:0] in_3,
  output Overflow,
  output Carry_Flag,
  output Equal,
  output [31:0] Result,
  output [31:0] Helper_Result,
  output Zero_Flag
);

  wire comparator_1_lt, comparator_2_lt, rnd_Clock;
  wire [1:0] n32_bit_adder_with_overflow_detection_1_out_5,
       n32_bit_subtractor_with_overflow_detection_1_out_5;
  wire [31:0] and_1_out, bit_extender_1_out, bit_extender_2_out, divider_1_out, divider_1_rem, divider_2_out,
       divider_2_rem, multiplier_1_cout, multiplier_1_out, multiplier_2_cout, multiplier_2_out,
       n32_bit_adder_with_overflow_detection_1_out_6, n32_bit_subtractor_with_overflow_detection_1_out_6,
       nor_1_out, or_1_out, random_1_out, shifter_1_out, shifter_2_out, shifter_3_out, xor_1_out;

  // Probe on in_1
  // Probe on in_1
  // Probe on in_2
  // Probe on in_2
  Clock clock_1 (.out(rnd_Clock));
  // Probe on in_3
  _32_bit_Adder_With_Overflow_Detection u_32_bit_adder_with_overflow_detection_1 (
    .out_4(n32_bit_adder_with_overflow_detection_1_out_5[1]),
    .out_5(n32_bit_adder_with_overflow_detection_1_out_5[0]), .in_1(in_1), .in_2(in_2),
    .out_6(n32_bit_adder_with_overflow_detection_1_out_6));  // open: in_3
  _32_bit_Subtractor_With_Overflow_Detection u_32_bit_subtractor_with_overflow_detection_1 (
    .out_4(n32_bit_subtractor_with_overflow_detection_1_out_5[1]),
    .out_5(n32_bit_subtractor_with_overflow_detection_1_out_5[0]), .in_1(in_1), .in_2(in_2),
    .out_6(n32_bit_subtractor_with_overflow_detection_1_out_6));  // open: in_3
  Shifter #(.width(32)) shifter_1 (.in(in_1), .\dist (in_2[4:0]), .out(shifter_1_out));
  Shifter #(.width(32), .shift("lr")) shifter_2 (.in(in_1), .\dist (in_2[4:0]), .out(shifter_2_out));
  assign and_1_out = in_1 & in_2;  // AND_Gate and_1, 32 bits wide
  Shifter #(.width(32), .shift("ar")) shifter_3 (.in(in_1), .\dist (in_2[4:0]), .out(shifter_3_out));
  assign or_1_out = in_1 | in_2;  // OR_Gate or_1, 32 bits wide
  assign nor_1_out = ~(in_1 | in_2);  // NOR_Gate nor_1, 32 bits wide
  assign xor_1_out = in_1 ^ in_2;  // XOR_Gate xor_1, 32 bits wide
  Comparator #(.width(32)) comparator_1 (.a(in_1), .b(in_2), .lt(comparator_1_lt));  // open: gt, eq
  Random #(.width(32)) random_1 (.clk(rnd_Clock), .next(1'b1), .out(random_1_out));  // open: clr
  Comparator #(.width(32), .mode("unsigned")) comparator_2 (
    .a(in_1), .b(in_2), .eq(Equal), .lt(comparator_2_lt));  // open: gt
  Multiplier #(.width(32)) multiplier_1 (
    .a(in_1), .b(in_2), .out(multiplier_1_out), .cout(multiplier_1_cout));  // open: cin
  Divider #(.width(32)) divider_1 (.a(in_1), .b(in_2), .out(divider_1_out), .rem(divider_1_rem));  // open: upper
  Multiplier #(.width(32)) multiplier_2 (
    .a(in_1), .b(in_2), .out(multiplier_2_out), .cout(multiplier_2_cout));  // open: cin
  Divider #(.width(32)) divider_2 (.a(in_1), .b(in_2), .out(divider_2_out), .rem(divider_2_rem));  // open: upper
  // Probe on Result
  // Probe on Result
  Multiplexer #(.select(4), .width(2)) multiplexer_1 (
    .in0(n32_bit_adder_with_overflow_detection_1_out_5),
    .in1(n32_bit_subtractor_with_overflow_detection_1_out_5), .in2(2'b00), .in3(2'b00), .in4(2'b00),
    .in5(2'b00), .in6(2'b00), .in7(2'b00), .in8(2'b00), .in9(2'b00), .in10(2'b00), .in11(2'b00),
    .in12(2'b00), .in13(2'b00), .in14(2'b00), .in15(2'b00), .out({Overflow, Carry_Flag}), .sel(in_3));  // open: en
  // Probe on Helper_Result
  assign bit_extender_1_out = {{31{1'b0}}, comparator_1_lt};  // Bit_Extender bit_extender_1
  assign bit_extender_2_out = {{31{1'b0}}, comparator_2_lt};  // Bit_Extender bit_extender_2
  Multiplexer #(.select(4), .width(32)) multiplexer_2 (
    .in0({32{1'b0}}), .in1({32{1'b0}}), .in2({32{1'b0}}), .in3({32{1'b0}}), .in4({32{1'b0}}),
    .in5({32{1'b0}}), .in6({32{1'b0}}), .in7({32{1'b0}}), .in8({32{1'b0}}), .in9({32{1'b0}}),
    .in10({32{1'b0}}), .in11({32{1'b0}}), .in12(multiplier_1_cout), .in13(divider_1_rem),
    .in14(multiplier_2_cout), .in15(divider_2_rem), .out(Helper_Result), .sel(in_3));  // open: en
  Multiplexer #(.select(4), .width(32)) multiplexer_3 (
    .in0(n32_bit_adder_with_overflow_detection_1_out_6),
    .in1(n32_bit_subtractor_with_overflow_detection_1_out_6), .in2(shifter_1_out), .in3(shifter_2_out),
    .in4(and_1_out), .in5(shifter_3_out), .in6(or_1_out), .in7(nor_1_out), .in8(xor_1_out),
    .in9(bit_extender_1_out), .in10(random_1_out), .in11(bit_extender_2_out), .in12(multiplier_1_out),
    .in13(divider_1_out), .in14(multiplier_2_out), .in15(divider_2_out), .out(Result), .sel(in_3));  // open: en
  Comparator #(.width(32)) comparator_3 (.a({32{1'b0}}), .b(Result), .eq(Zero_Flag));  // open: gt, lt

  // Other names for the same wires on the sheet: CF = Carry_Flag; OF = Overflow; A[31:0] = in_1; B[31:0] = in_2;
  //   Help_Result[31:0] = Helper_Result; Main_Result[31:0] = Result; OP[3:0] = in_3; Zero = Zero_Flag

  // Notes on the sheet:
  //   INPUTS
  //   Added With OF
  //   Substractor With OF
  //   AND
  //   OR
  //   NOR
  //   XOR
  //   Set Less Than
  //   Set Random
  //   Set Less Than(U)
  //   Signed Mult
  //   Signed Div
  //   Unsigned Mult
  //   Unsigned Div
  //   Logical Left
  //   Logical Right
  //   Arithmetic Right
  //   OUTPUTS
endmodule

module ALU_Decoder (
  input  [5:0] Op_Code,
  input  [5:0] Func_Code,
  input  Sum,
  output [3:0] ALU_operation,
  output Write_Hi___Lo
);

  wire and_4_out;
  wire [1:0] nor_1_out;
  wire [2:2] or_1_out;
  wire [3:0] and_3_out, multiplexer_1_out, multiplexer_2_out;

  and and_1 (and_3_out[3], Op_Code[3], Op_Code[1]);
  and and_2 (and_3_out[2], Op_Code[2], ~Op_Code[1]);  // AND_Gate
  and and_3 (and_3_out[0], Op_Code[3], ~Op_Code[2], Op_Code[1]);  // AND_Gate
  or or_1 (or_1_out[2], Func_Code[2], Func_Code[4]);
  Multiplexer #(.width(4), .enable("false")) multiplexer_1 (
    .in0(4'b1001), .in1({and_3_out[3:2], Op_Code[0], and_3_out[0]}), .out(multiplexer_1_out), .sel(Op_Code[3]));
  and and_4 (and_4_out, Func_Code[3], Func_Code[4], ~Func_Code[5]);  // AND_Gate
  Multiplexer #(.select(2), .width(4), .enable("false")) multiplexer_2 (
    .in0(multiplexer_1_out), .in1({Func_Code[3], or_1_out[2], Func_Code[0], Func_Code[1]}),
    .in2(Func_Code[3:0]), .in3(Func_Code[3:0]), .out(multiplexer_2_out), .sel(nor_1_out));
  and and_5 (nor_1_out[1], Op_Code[5], Op_Code[4], Op_Code[3], ~Op_Code[2], ~Op_Code[1], ~Op_Code[0]);  // AND_Gate
  Multiplexer #(.width(4), .enable("false")) multiplexer_3 (
    .in0(multiplexer_2_out), .in1(4'b0000), .out(ALU_operation), .sel(Sum));
  nor nor_1 (nor_1_out[0], Op_Code[5], Op_Code[4], Op_Code[3], Op_Code[2], Op_Code[1], Op_Code[0], 1'b0);
  and and_6 (Write_Hi___Lo, nor_1_out[0], and_4_out);

  // Notes on the sheet:
  //   Operation
  //   add
  //   sub
  //   logical left
  //   logical right
  //   and
  //   arithmetic right
  //   or
  //   nor
  //   xor
  //   slt
  //   rnd (Op 11 1111)
  //   sltu
  //   mult
  //   div
  //   mulu
  //   divu
  //   OP-Code: 00 0000
  //   Func-Code
  //   10 0000
  //   10 0010
  //   10 0001
  //   10 0011
  //   10 0100
  //   10 0110
  //   10 0101
  //   10 0111
  //   10 1000
  //   10 1010
  //   00 0010
  //   10 1011
  //   01 1000
  //   01 1010
  //   01 1001
  //   01 1011
  //   0001
  //   0010
  //   0011
  //   ALU-Op
  //   0000
  //   0100
  //   0101
  //   0110
  //   0111
  //   1000
  //   1001
  //   1010
  //   1011
  //   1100
  //   1101
  //   1110
  //   1111
  //   Operation
  //   beq
  //   bne
  //   blez
  //   bgtz
  //   bltz
  //   Operation
  //   addi
  //   andi
  //   ori
  //   xori
  //   slti
  //   sltiu
  //   ALU-Op: 1001
  //   Op-Code
  //   00 0100
  //   00 0101
  //   00 0110
  //   00 0111
  //   00 0001
  //   Op-Code
  //   00 1000
  //   00 1100
  //   00 1101
  //   00 1110
  //   00 1010
  //   00 1011
  //   ALU-Op
  //   0000
  //   0100
  //   0110
  //   1000
  //   1001
  //   1011
  //   Op-Code: 11 1000
  //   Operation
  //   pop
  //   push
  //   ALU-Op
  //   0000
  //   0001
endmodule

// RF
module Register_File (
  input  [4:0] in_1,
  input  [4:0] in_2,
  input  [4:0] in_3,
  input  [31:0] in_4,
  input  in_5,
  input  in_6,
  input  in_7,
  output [31:0] R1,
  output [31:0] R2
);

  wire decoder_1_out0, decoder_1_out1, decoder_1_out2, decoder_1_out3, decoder_2_out0, decoder_2_out1,
       decoder_2_out2, decoder_2_out3, decoder_2_out4, decoder_2_out5, decoder_2_out6, decoder_2_out7,
       decoder_3_out0, decoder_3_out1, decoder_3_out2, decoder_3_out3, decoder_3_out4, decoder_3_out5,
       decoder_3_out6, decoder_3_out7, decoder_4_out0, decoder_4_out1, decoder_4_out2, decoder_4_out3,
       decoder_4_out4, decoder_4_out5, decoder_4_out6, decoder_4_out7, decoder_5_out0, decoder_5_out1,
       decoder_5_out2, decoder_5_out3, decoder_5_out4, decoder_5_out5, decoder_5_out6, decoder_5_out7;
  wire [31:0] register_1_q, register_2_q, register_3_q, register_4_q, register_5_q, register_6_q,
       register_7_q, register_8_q, register_9_q, register_10_q, register_11_q, register_12_q, register_13_q,
       register_14_q, register_15_q, register_16_q, register_17_q, register_18_q, register_19_q,
       register_20_q, register_21_q, register_22_q, register_23_q, register_24_q, register_25_q,
       register_26_q, register_27_q, register_28_q, register_29_q, register_30_q, register_31_q,
       register_32_q;

  Decoder #(.select(2), .disabled(0)) decoder_1 (
    .out0(decoder_1_out0), .out1(decoder_1_out1), .out2(decoder_1_out2), .out3(decoder_1_out3),
    .sel(in_3[4:3]), .en(in_5));
  Decoder #(.select(3), .disabled(0)) decoder_2 (
    .out0(decoder_2_out0), .out1(decoder_2_out1), .out2(decoder_2_out2), .out3(decoder_2_out3),
    .out4(decoder_2_out4), .out5(decoder_2_out5), .out6(decoder_2_out6), .out7(decoder_2_out7),
    .sel(in_3[2:0]), .en(decoder_1_out0));
  Decoder #(.select(3), .disabled(0)) decoder_3 (
    .out0(decoder_3_out0), .out1(decoder_3_out1), .out2(decoder_3_out2), .out3(decoder_3_out3),
    .out4(decoder_3_out4), .out5(decoder_3_out5), .out6(decoder_3_out6), .out7(decoder_3_out7),
    .sel(in_3[2:0]), .en(decoder_1_out1));
  Decoder #(.select(3), .disabled(0)) decoder_4 (
    .out0(decoder_4_out0), .out1(decoder_4_out1), .out2(decoder_4_out2), .out3(decoder_4_out3),
    .out4(decoder_4_out4), .out5(decoder_4_out5), .out6(decoder_4_out6), .out7(decoder_4_out7),
    .sel(in_3[2:0]), .en(decoder_1_out2));
  Decoder #(.select(3), .disabled(0)) decoder_5 (
    .out0(decoder_5_out0), .out1(decoder_5_out1), .out2(decoder_5_out2), .out3(decoder_5_out3),
    .out4(decoder_5_out4), .out5(decoder_5_out5), .out6(decoder_5_out6), .out7(decoder_5_out7),
    .sel(in_3[2:0]), .en(decoder_1_out3));
  Register #(.width(32), .trigger("falling")) register_1 (
    .D(in_4), .en(decoder_4_out0), .Q(register_1_q), .clk(in_6), .clr(in_7));
  Register #(.width(32), .trigger("falling")) register_2 (
    .D(in_4), .en(decoder_5_out0), .Q(register_2_q), .clk(in_6), .clr(in_7));
  Register #(.width(32), .trigger("falling")) register_3 (
    .D(in_4), .en(decoder_2_out0), .Q(register_3_q), .clr(in_7));  // open: clk
  Register #(.width(32), .trigger("falling")) register_4 (
    .D(in_4), .en(decoder_3_out0), .Q(register_4_q), .clk(in_6), .clr(in_7));
  Register #(.width(32), .trigger("falling")) register_5 (
    .D(in_4), .en(decoder_2_out1), .Q(register_5_q), .clk(in_6), .clr(in_7));
  Register #(.width(32), .trigger("falling")) register_6 (
    .D(in_4), .en(decoder_3_out1), .Q(register_6_q), .clk(in_6), .clr(in_7));
  Register #(.width(32), .trigger("falling")) register_7 (
    .D(in_4), .en(decoder_4_out1), .Q(register_7_q), .clk(in_6), .clr(in_7));
  Register #(.width(32), .trigger("falling")) register_8 (
    .D(in_4), .en(decoder_5_out1), .Q(register_8_q), .clk(in_6), .clr(in_7));
  Register #(.width(32), .trigger("falling")) register_9 (
    .D(in_4), .en(decoder_2_out2), .Q(register_9_q), .clk(in_6), .clr(in_7));
  Register #(.width(32), .trigger("falling")) register_10 (
    .D(in_4), .en(decoder_3_out2), .Q(register_10_q), .clk(in_6), .clr(in_7));
  Register #(.width(32), .trigger("falling")) register_11 (
    .en(decoder_4_out2), .Q(register_11_q), .clk(in_6), .clr(in_7));  // open: D
  Register #(.width(32), .trigger("falling")) register_12 (
    .D(in_4), .en(decoder_5_out2), .Q(register_12_q), .clk(in_6), .clr(in_7));
  Register #(.width(32), .trigger("falling")) register_13 (
    .D(in_4), .en(decoder_2_out3), .Q(register_13_q), .clk(in_6), .clr(in_7));
  Register #(.width(32), .trigger("falling")) register_14 (
    .D(in_4), .en(decoder_3_out3), .Q(register_14_q), .clk(in_6), .clr(in_7));
  Register #(.width(32), .trigger("falling")) register_15 (
    .en(decoder_4_out3), .Q(register_15_q), .clk(in_6), .clr(in_7));  // open: D
  Register #(.width(32), .trigger("falling")) register_16 (
    .D(in_4), .en(decoder_5_out3), .Q(register_16_q), .clk(in_6), .clr(in_7));
  Register #(.width(32), .trigger("falling")) register_17 (
    .en(decoder_4_out4), .Q(register_17_q), .clk(in_6), .clr(in_7));  // open: D
  Register #(.width(32), .trigger("falling")) register_18 (
    .D(in_4), .en(decoder_5_out4), .Q(register_18_q), .clk(in_6), .clr(in_7));
  Register #(.width(32), .trigger("falling")) register_19 (
    .D(in_4), .en(decoder_2_out4), .Q(register_19_q), .clk(in_6), .clr(in_7));
  Register #(.width(32), .trigger("falling")) register_20 (
    .D(in_4), .en(decoder_3_out4), .Q(register_20_q), .clk(in_6), .clr(in_7));
  Register #(.width(32), .trigger("falling")) register_21 (
    .D(in_4), .en(decoder_2_out5), .Q(register_21_q), .clk(in_6), .clr(in_7));
  Register #(.width(32), .trigger("falling")) register_22 (
    .D(in_4), .en(decoder_3_out5), .Q(register_22_q), .clk(in_6), .clr(in_7));
  Register #(.width(32), .trigger("falling")) register_23 (
    .en(decoder_4_out5), .Q(register_23_q), .clk(in_6), .clr(in_7));  // open: D
  Register #(.width(32), .trigger("falling")) register_24 (
    .D(in_4), .en(decoder_5_out5), .Q(register_24_q), .clk(in_6), .clr(in_7));
  Register #(.width(32), .trigger("falling")) register_25 (
    .D(in_4), .en(decoder_2_out6), .Q(register_25_q), .clk(in_6), .clr(in_7));
  Register #(.width(32), .trigger("falling")) register_26 (
    .D(in_4), .en(decoder_3_out6), .Q(register_26_q), .clk(in_6), .clr(in_7));
  Register #(.width(32), .trigger("falling")) register_27 (
    .en(decoder_4_out6), .Q(register_27_q), .clk(in_6), .clr(in_7));  // open: D
  Register #(.width(32), .trigger("falling")) register_28 (
    .D(in_4), .en(decoder_5_out6), .Q(register_28_q), .clk(in_6), .clr(in_7));
  Register #(.width(32), .trigger("falling")) register_29 (
    .D(in_4), .en(decoder_2_out7), .Q(register_29_q), .clk(in_6), .clr(in_7));
  Register #(.width(32), .trigger("falling")) register_30 (
    .D(in_4), .en(decoder_3_out7), .Q(register_30_q), .clk(in_6), .clr(in_7));
  Register #(.width(32), .trigger("falling")) register_31 (
    .en(decoder_4_out7), .Q(register_31_q), .clk(in_6), .clr(in_7));  // open: D
  Register #(.width(32), .trigger("falling")) register_32 (
    .D(in_4), .en(decoder_5_out7), .Q(register_32_q), .clk(in_6), .clr(in_7));
  Multiplexer #(.select(5), .width(32)) multiplexer_1 (
    .in0(register_3_q), .in1(register_5_q), .in2(register_9_q), .in3(register_13_q), .in4(register_19_q),
    .in5(register_21_q), .in6(register_25_q), .in7(register_29_q), .in8(register_4_q), .in9(register_6_q),
    .in10(register_10_q), .in11(register_14_q), .in12(register_20_q), .in13(register_22_q),
    .in14(register_26_q), .in15(register_30_q), .in16(register_1_q), .in17(register_7_q),
    .in18(register_11_q), .in19(register_15_q), .in20(register_17_q), .in21(register_23_q),
    .in22(register_27_q), .in23(register_31_q), .in24(register_2_q), .in25(register_8_q),
    .in26(register_12_q), .in27(register_16_q), .in28(register_18_q), .in29(register_24_q),
    .in30(register_28_q), .in31(register_32_q), .out(R1), .sel(in_1));  // open: en
  Multiplexer #(.select(5), .width(32)) multiplexer_2 (
    .in0(register_3_q), .in1(register_5_q), .in2(register_9_q), .in3(register_13_q), .in4(register_19_q),
    .in5(register_21_q), .in6(register_25_q), .in7(register_29_q), .in8(register_4_q), .in9(register_6_q),
    .in10(register_10_q), .in11(register_14_q), .in12(register_20_q), .in13(register_22_q),
    .in14(register_26_q), .in15(register_30_q), .in16(register_1_q), .in17(register_7_q),
    .in18(register_11_q), .in19(register_15_q), .in20(register_17_q), .in21(register_23_q),
    .in22(register_27_q), .in23(register_31_q), .in24(register_2_q), .in25(register_8_q),
    .in26(register_12_q), .in27(register_16_q), .in28(register_18_q), .in29(register_24_q),
    .in30(register_28_q), .in31(register_32_q), .out(R2), .sel(in_2));  // open: en

  // Other names for the same wires on the sheet: Clock = in_6; Dest_Address[4:0] = in_3; IN_Reg1[4:0] = in_1;
  //   IN_Reg_2[4:0] = in_2; Input_Data[31:0] = in_4; OUT_Reg1[31:0] = R1; OUT_Reg2[31:0] = R2; Reset = in_7;
  //   Write_Enable = in_5

  // Notes on the sheet:
  //   INPUTS
  //   OUTPUTS
endmodule

module Chronometer (
  input  in_1,
  input  in_2,
  input  in_3,
  input  [3:0] in_4,
  output Counting,
  output Cicle_Finished
);

  wire comparator_1_eq, d_ff_1_q, or_1_out;
  wire [4:0] counter_1_q;

  Clock clock_1 ();  // open: out
  Counter #(.width(5), .max('h1f)) counter_1 (
    .load(1'b0), .count(in_2), .Q(counter_1_q), .clk(in_1), .clr(or_1_out));  // open: D, carry
  Comparator #(.width(5)) comparator_1 (.a(counter_1_q), .b({5{1'b0}}), .eq(comparator_1_eq));  // open: gt, lt
  Comparator #(.width(5)) comparator_2 (.a({1'b0, in_4}), .b(counter_1_q), .eq(Cicle_Finished));  // open: gt, lt
  or or_1 (or_1_out, d_ff_1_q, in_3);
  or or_2 (Counting, ~comparator_1_eq, in_2);  // OR_Gate
  D_Flip_Flop #(.trigger("falling")) d_ff_1 (
    .clk(in_1), .D(Cicle_Finished), .Q(d_ff_1_q), .reset(or_1_out));  // open: Qn, preset, en

  // Other names for the same wires on the sheet: Frecuency[3:0] = in_4; Clock = in_1; END = Cicle_Finished;
  //   Reset_Signal = in_3; Start_Signal = in_2

  // Notes on the sheet:
  //   INPUTS
  //   OUTPUTS
endmodule

module Program_Counter (
  input  [3:0] in_1,
  input  in_2,
  input  in_3,
  input  in_4,
  input  in_5,
  input  [31:0] in_6,
  input  [31:0] in_7,
  input  [31:0] in_8,
  input  [31:0] in_9,
  input  [1:0] Ram_selector,
  input  in_11,
  output [31:0] out_12,
  output [31:0] out_13
);

  wire and_1_out, chronometer_1_cicle_finished, chronometer_1_counting, Enable, not_1_out, or_2_out;

  Clock clock_1 ();  // open: out
  or or_1 (Enable, in_3, in_4, in_5);
  Multiplexer #(.select(2), .width(32)) multiplexer_1 (
    .in0(in_6), .in1(in_7), .in2(in_8), .in3(in_9), .out(out_12), .sel(Ram_selector));  // open: en
  Multiplexer #(.width(32)) multiplexer_2 (.in0(32'hffff0010), .in1(out_12), .out(out_13), .sel(or_2_out));  // open: en
  or or_2 (or_2_out, in_11, Enable, and_1_out);
  not not_1 (not_1_out, in_11);
  and and_1 (and_1_out, ~chronometer_1_cicle_finished, chronometer_1_counting);  // AND_Gate
  Chronometer chronometer_1 (
    .in_2(not_1_out), .in_3(Enable), .in_4(in_1), .Counting(chronometer_1_counting),
    .Cicle_Finished(chronometer_1_cicle_finished), .in_1(in_2));

  // Other names for the same wires on the sheet: Clock = in_2; Read_Time[3:0] = in_1; Reset = in_3

  // Notes on the sheet:
  //   Enable Signals
  //   Ram Imputs
  //   INPUTS
  //   Jump
  //   Actual Queue
  //   Next Instruction
  //   Actual Queue
  //   OUTPUTS
  //   Next Instruction
endmodule

module _32_bit_Adder_With_Overflow_Detection (
  input  [31:0] in_1,
  input  [31:0] in_2,
  input  in_3,
  output out_4,
  output out_5,
  output [31:0] out_6
);

  wire adder_1_cout;

  // Probe on in_1
  Adder #(.width(31)) adder_1 (.a(in_1[30:0]), .b(in_2[30:0]), .out(out_6[30:0]), .cin(in_3), .cout(adder_1_cout));
  Adder #(.width(1)) adder_2 (.a(in_1[31]), .b(in_2[31]), .out(out_6[31]), .cin(adder_1_cout), .cout(out_4));
  // Probe on in_2
  xor xor_1 (out_5, adder_1_cout, out_4);
  // Probe on out_6

  // Other names for the same wires on the sheet: A[31:0] = in_1; B[31:0] = in_2; c_in = in_3; CF = out_4; OF = out_5;
  //   Result[31:0] = out_6
endmodule

module _32_bit_Subtractor_With_Overflow_Detection (
  input  [31:0] in_1,
  input  [31:0] in_2,
  input  in_3,
  output out_4,
  output out_5,
  output [31:0] out_6
);

  wire subtractor_1_bout;

  // Probe on in_1
  Subtractor #(.width(31)) subtractor_1 (
    .a(in_1[30:0]), .b(in_2[30:0]), .out(out_6[30:0]), .bin(in_3), .bout(subtractor_1_bout));
  Subtractor #(.width(1)) subtractor_2 (
    .a(in_1[31]), .b(in_2[31]), .out(out_6[31]), .bin(subtractor_1_bout), .bout(out_4));
  // Probe on in_2
  xor xor_1 (out_5, subtractor_1_bout, out_4);
  // Probe on out_6

  // Other names for the same wires on the sheet: A[31:0] = in_1; B[31:0] = in_2; b_in = in_3; CF = out_4; OF = out_5;
  //   Result[31:0] = out_6
endmodule

module _32_bit_Un_signed_Multiplier (
  input  [31:0] in_1,
  input  [31:0] in_2,
  output [31:0] out_3,
  output [31:0] out_4
);

  wire [31:0] adder_1_out, adder_2_out, multiplexer_1_out, multiplexer_2_out, multiplier_1_cout,
       multiplier_1_out, n32_bit_absolute_value_1_output, n32_bit_absolute_value_2_output, not_1_out,
       not_2_out;

  // Probe on in_1
  assign not_1_out = ~in_1;  // NOT_Gate not_1, 32 bits wide
  assign not_2_out = ~in_2;  // NOT_Gate not_2, 32 bits wide
  _32_bit_Absolute_value u_32_bit_absolute_value_1 (.in_1(in_1), .Output(n32_bit_absolute_value_1_output));
  _32_bit_Absolute_value u_32_bit_absolute_value_2 (.in_1(in_2), .Output(n32_bit_absolute_value_2_output));
  Multiplexer #(.width(32)) multiplexer_1 (
    .in0(in_1), .in1(adder_1_out), .out(multiplexer_1_out), .sel(in_1[31]));  // open: en
  Adder #(.width(32)) adder_1 (.a(not_1_out), .b(32'h1), .out(adder_1_out));  // open: cin, cout
  Multiplexer #(.width(32)) multiplexer_2 (
    .in0(in_2), .in1(adder_2_out), .out(multiplexer_2_out), .sel(in_2[31]));  // open: en
  Adder #(.width(32)) adder_2 (.a(not_2_out), .b(32'h1), .out(adder_2_out));  // open: cin, cout
  // Probe on in_2
  Multiplier #(.width(32)) multiplier_1 (
    .a(multiplexer_1_out), .b(multiplexer_2_out), .out(multiplier_1_out), .cout(multiplier_1_cout));  // open: cin
  // Probe on out_3
  Multiplier #(.width(32)) multiplier_2 (
    .a(n32_bit_absolute_value_1_output), .b(n32_bit_absolute_value_2_output), .out(out_4), .cout(out_3));  // open: cin
  // Probe on out_4

  // Other names for the same wires on the sheet: A[31:0] = in_1; B[31:0] = in_2; Result_1[31:0] = out_4;
  //   Result_2[31:0] = out_3

  // Notes on the sheet:
  //   LEGACY
endmodule

module _32_bit_Un_signed_Divider (
  input  [31:0] in_1,
  input  [31:0] in_2,
  output [31:0] out_3,
  output [31:0] out_4
);

  wire [31:0] n32_bit_absolute_value_1_output, n32_bit_absolute_value_2_output;

  // Probe on in_1
  _32_bit_Absolute_value u_32_bit_absolute_value_1 (.in_1(in_1), .Output(n32_bit_absolute_value_1_output));
  _32_bit_Absolute_value u_32_bit_absolute_value_2 (.in_1(in_2), .Output(n32_bit_absolute_value_2_output));
  // Probe on in_2
  // Probe on out_3
  Divider #(.width(32)) divider_1 (
    .a(n32_bit_absolute_value_1_output), .b(n32_bit_absolute_value_2_output), .out(out_3), .rem(out_4));  // open: upper
  // Probe on out_4

  // Other names for the same wires on the sheet: A[31:0] = in_1; B[31:0] = in_2; Result_1[31:0] = out_3;
  //   Result_2[31:0] = out_4
endmodule

module _32_bit_Absolute_value (
  input  [31:0] in_1,
  output [31:0] Output
);

  wire [31:0] adder_1_out, not_1_out;

  // Probe on in_1
  assign not_1_out = ~in_1;  // NOT_Gate not_1, 32 bits wide
  _16_to_32_bit_sign_extender u_16_to_32_bit_sign_extender_1 ();  // open: in_1, Outx4, Out
  Multiplexer #(.width(32)) multiplexer_1 (.in0(in_1), .in1(adder_1_out), .out(Output), .sel(in_1[31]));  // open: en
  Adder #(.width(32)) adder_1 (.a(not_1_out), .b(32'h1), .out(adder_1_out));  // open: cin, cout
  // Probe on Output
endmodule

module _16_to_32_bit_sign_extender (
  input  [15:0] in_1,
  output [31:0] Out,
  output [31:0] Outx4
);

  // Probe on in_1
  // Probe on {{17{in_1[15]}}, in_1[14:0]}
  // Probe on {{15{in_1[15]}}, in_1[14:0], 2'b00}

  assign Out = {{17{in_1[15]}}, in_1[14:0]};
  assign Outx4 = {{15{in_1[15]}}, in_1[14:0], 2'b00};
endmodule
